// Logisim project CPU1bywilliampring.circ as structural Verilog: 27 circuits, main circuit CPU A
module _16_Bit (
  input  A0,
  input  A1,
  input  A2,
  input  A3,
  output F0,
  output F1,
  output F2,
  output F3,
  output F4,
  output F5,
  output F6,
  output F7,
  output F8,
  output F9,
  output F10,
  output F11,
  output F12,
  output F13,
  output F14,
  output F15
);

  wire not_1_out, not_2_out, not_3_out, not_4_out;

  not not_1 (not_1_out, A0);
  not not_2 (not_2_out, A1);
  not not_3 (not_3_out, A2);
  not not_4 (not_4_out, A3);
  and _0000 (F0, not_1_out, not_2_out, not_3_out, not_4_out);
  and _0001 (F1, not_1_out, not_2_out, not_3_out, A3);
  and _0010 (F2, not_1_out, not_2_out, A2, not_4_out);
  and _0011 (F3, not_1_out, not_2_out, A2, A3);
  and _0100 (F4, not_1_out, A1, not_3_out, not_4_out);
  and _0101 (F5, not_1_out, A1, not_3_out, A3);
  and _0110 (F6, not_1_out, A1, A2, not_4_out);
  and _0111 (F7, not_1_out, A1, A2, A3);
  and _1000 (F8, A0, not_2_out, not_3_out, not_4_out);
  and _1001 (F9, A0, not_2_out, not_3_out, A3);
  and _1010 (F10, A0, not_2_out, A2, not_4_out);
  and _1011 (F11, A0, not_2_out, A2, A3);
  and _1100 (F12, A0, A1, not_3_out, not_4_out);
  and _1101 (F13, A0, A1, not_3_out, A3);
  and _1110 (F14, A0, A1, A2, not_4_out);
  and _1111 (F15, A0, A1, A2, A3);
endmodule

module SRAM_Memory_Cell (
  input  Input,
  input  WL,
  input  WR,
  output Output
);

  wire and_1_out, d_ff_1_q;

  and and_1 (and_1_out, WL, WR);
  D_Flip_Flop d_ff_1 (.clk(and_1_out), .D(Input), .Q(d_ff_1_q));  // open: Qn, preset, en, reset
  assign Output = WL ? d_ff_1_q : 1'bz;  // Controlled_Buffer controlled_buffer_1
endmodule

module SRAM_Memory_Circuit (
  input  DI1,
  input  DI0,
  input  A1,
  input  A0,
  input  WE_Write_Enable,
  input  CS_Chip_Select,
  input  OE_output_enable,
  output DO1,
  output DO0
);

  wire and_1_out, and_2_out, n4_bit_decoder_1_out_3, n4_bit_decoder_1_out_4, n4_bit_decoder_1_out_5,
       n4_bit_decoder_1_out_6, sram_memory_cell_1_output, sram_memory_cell_5_output;

  _4_Bit_decoder u_4_bit_decoder_1 (
    .A(A1), .B(A0), .out_3(n4_bit_decoder_1_out_3), .out_4(n4_bit_decoder_1_out_4),
    .out_5(n4_bit_decoder_1_out_5), .out_6(n4_bit_decoder_1_out_6));
  and and_1 (and_1_out, WE_Write_Enable, CS_Chip_Select);
  and and_2 (and_2_out, CS_Chip_Select, OE_output_enable);
  SRAM_Memory_Cell sram_memory_cell_1 (
    .Input(DI1), .WL(n4_bit_decoder_1_out_3), .WR(and_1_out), .Output(sram_memory_cell_1_output));
  SRAM_Memory_Cell sram_memory_cell_2 (
    .Input(DI1), .WL(n4_bit_decoder_1_out_4), .WR(and_1_out), .Output(sram_memory_cell_1_output));
  SRAM_Memory_Cell sram_memory_cell_3 (
    .Input(DI1), .WL(n4_bit_decoder_1_out_5), .WR(and_1_out), .Output(sram_memory_cell_1_output));
  SRAM_Memory_Cell sram_memory_cell_4 (
    .Input(DI1), .WL(n4_bit_decoder_1_out_6), .WR(and_1_out), .Output(sram_memory_cell_1_output));
  assign DO1 = and_2_out ? sram_memory_cell_1_output : 1'bz;  // Controlled_Buffer controlled_buffer_1
  SRAM_Memory_Cell sram_memory_cell_5 (
    .Input(DI0), .WL(n4_bit_decoder_1_out_3), .WR(and_1_out), .Output(sram_memory_cell_5_output));
  SRAM_Memory_Cell sram_memory_cell_6 (
    .Input(DI0), .WL(n4_bit_decoder_1_out_4), .WR(and_1_out), .Output(sram_memory_cell_5_output));
  SRAM_Memory_Cell sram_memory_cell_7 (
    .Input(DI0), .WL(n4_bit_decoder_1_out_5), .WR(and_1_out), .Output(sram_memory_cell_5_output));
  SRAM_Memory_Cell sram_memory_cell_8 (
    .Input(DI0), .WL(n4_bit_decoder_1_out_6), .WR(and_1_out), .Output(sram_memory_cell_5_output));
  assign DO0 = and_2_out ? sram_memory_cell_5_output : 1'bz;  // Controlled_Buffer controlled_buffer_2
endmodule

// Memory Cell
module Memory_Circuit (
  input  DI0,
  input  DI1,
  input  DI2,
  input  DI3,
  input  DI4,
  input  DI5,
  input  A0,
  input  A1,
  input  A2,
  input  A3,
  input  WE_Write_Enable,
  input  CS_Chip_Select,
  input  OE_output_enable,
  output DO5,
  output DO4,
  output DO3,
  output DO2,
  output DO1,
  output DO0
);

  wire and_1_out, and_2_out, n16_bit_1_f0, n16_bit_1_f1, n16_bit_1_f2, n16_bit_1_f3, n16_bit_1_f4,
       n16_bit_1_f5, n16_bit_1_f6, n16_bit_1_f7, n16_bit_1_f8, n16_bit_1_f9, n16_bit_1_f10, n16_bit_1_f11,
       n16_bit_1_f12, n16_bit_1_f13, n16_bit_1_f14, n16_bit_1_f15, sram_memory_cell_1_output,
       sram_memory_cell_17_output, sram_memory_cell_33_output, sram_memory_cell_49_output,
       sram_memory_cell_65_output, sram_memory_cell_81_output;

  _16_Bit u_16_bit_1 (
    .A0(A0), .A1(A1), .A2(A2), .A3(A3), .F0(n16_bit_1_f0), .F1(n16_bit_1_f1), .F2(n16_bit_1_f2),
    .F3(n16_bit_1_f3), .F4(n16_bit_1_f4), .F5(n16_bit_1_f5), .F6(n16_bit_1_f6), .F7(n16_bit_1_f7),
    .F8(n16_bit_1_f8), .F9(n16_bit_1_f9), .F10(n16_bit_1_f10), .F11(n16_bit_1_f11), .F12(n16_bit_1_f12),
    .F13(n16_bit_1_f13), .F14(n16_bit_1_f14), .F15(n16_bit_1_f15));
  and and_1 (and_1_out, WE_Write_Enable, CS_Chip_Select);
  SRAM_Memory_Cell sram_memory_cell_1 (
    .Input(DI5), .WL(n16_bit_1_f0), .WR(and_1_out), .Output(sram_memory_cell_1_output));
  SRAM_Memory_Cell sram_memory_cell_2 (
    .Input(DI5), .WL(n16_bit_1_f1), .WR(and_1_out), .Output(sram_memory_cell_1_output));
  SRAM_Memory_Cell sram_memory_cell_3 (
    .Input(DI5), .WL(n16_bit_1_f2), .WR(and_1_out), .Output(sram_memory_cell_1_output));
  SRAM_Memory_Cell sram_memory_cell_4 (
    .Input(DI5), .WL(n16_bit_1_f3), .WR(and_1_out), .Output(sram_memory_cell_1_output));
  SRAM_Memory_Cell sram_memory_cell_5 (
    .Input(DI5), .WL(n16_bit_1_f4), .WR(and_1_out), .Output(sram_memory_cell_1_output));
  SRAM_Memory_Cell sram_memory_cell_6 (
    .Input(DI5), .WL(n16_bit_1_f5), .WR(and_1_out), .Output(sram_memory_cell_1_output));
  SRAM_Memory_Cell sram_memory_cell_7 (
    .Input(DI5), .WL(n16_bit_1_f6), .WR(and_1_out), .Output(sram_memory_cell_1_output));
  SRAM_Memory_Cell sram_memory_cell_8 (
    .Input(DI5), .WL(n16_bit_1_f7), .WR(and_1_out), .Output(sram_memory_cell_1_output));
  SRAM_Memory_Cell sram_memory_cell_9 (
    .Input(DI5), .WL(n16_bit_1_f8), .WR(and_1_out), .Output(sram_memory_cell_1_output));
  SRAM_Memory_Cell sram_memory_cell_10 (
    .Input(DI5), .WL(n16_bit_1_f9), .WR(and_1_out), .Output(sram_memory_cell_1_output));
  SRAM_Memory_Cell sram_memory_cell_11 (
    .Input(DI5), .WL(n16_bit_1_f10), .WR(and_1_out), .Output(sram_memory_cell_1_output));
  SRAM_Memory_Cell sram_memory_cell_12 (
    .Input(DI5), .WL(n16_bit_1_f11), .WR(and_1_out), .Output(sram_memory_cell_1_output));
  SRAM_Memory_Cell sram_memory_cell_13 (
    .Input(DI5), .WL(n16_bit_1_f12), .WR(and_1_out), .Output(sram_memory_cell_1_output));
  SRAM_Memory_Cell sram_memory_cell_14 (
    .Input(DI5), .WL(n16_bit_1_f13), .WR(and_1_out), .Output(sram_memory_cell_1_output));
  SRAM_Memory_Cell sram_memory_cell_15 (
    .Input(DI5), .WL(n16_bit_1_f14), .WR(and_1_out), .Output(sram_memory_cell_1_output));
  SRAM_Memory_Cell sram_memory_cell_16 (
    .Input(DI5), .WL(n16_bit_1_f15), .WR(and_1_out), .Output(sram_memory_cell_1_output));
  and and_2 (and_2_out, CS_Chip_Select, OE_output_enable);
  assign DO5 = and_2_out ? sram_memory_cell_1_output : 1'bz;  // Controlled_Buffer controlled_buffer_1
  SRAM_Memory_Cell sram_memory_cell_17 (
    .Input(DI4), .WL(n16_bit_1_f0), .WR(and_1_out), .Output(sram_memory_cell_17_output));
  SRAM_Memory_Cell sram_memory_cell_18 (
    .Input(DI4), .WL(n16_bit_1_f1), .WR(and_1_out), .Output(sram_memory_cell_17_output));
  SRAM_Memory_Cell sram_memory_cell_19 (
    .Input(DI4), .WL(n16_bit_1_f2), .WR(and_1_out), .Output(sram_memory_cell_17_output));
  SRAM_Memory_Cell sram_memory_cell_20 (
    .Input(DI4), .WL(n16_bit_1_f3), .WR(and_1_out), .Output(sram_memory_cell_17_output));
  SRAM_Memory_Cell sram_memory_cell_21 (
    .Input(DI4), .WL(n16_bit_1_f4), .WR(and_1_out), .Output(sram_memory_cell_17_output));
  SRAM_Memory_Cell sram_memory_cell_22 (
    .Input(DI4), .WL(n16_bit_1_f5), .WR(and_1_out), .Output(sram_memory_cell_17_output));
  SRAM_Memory_Cell sram_memory_cell_23 (
    .Input(DI4), .WL(n16_bit_1_f6), .WR(and_1_out), .Output(sram_memory_cell_17_output));
  SRAM_Memory_Cell sram_memory_cell_24 (
    .Input(DI4), .WL(n16_bit_1_f7), .WR(and_1_out), .Output(sram_memory_cell_17_output));
  SRAM_Memory_Cell sram_memory_cell_25 (
    .Input(DI4), .WL(n16_bit_1_f8), .WR(and_1_out), .Output(sram_memory_cell_17_output));
  SRAM_Memory_Cell sram_memory_cell_26 (
    .Input(DI4), .WL(n16_bit_1_f9), .WR(and_1_out), .Output(sram_memory_cell_17_output));
  SRAM_Memory_Cell sram_memory_cell_27 (
    .Input(DI4), .WL(n16_bit_1_f10), .WR(and_1_out), .Output(sram_memory_cell_17_output));
  SRAM_Memory_Cell sram_memory_cell_28 (
    .Input(DI4), .WL(n16_bit_1_f11), .WR(and_1_out), .Output(sram_memory_cell_17_output));
  SRAM_Memory_Cell sram_memory_cell_29 (
    .Input(DI4), .WL(n16_bit_1_f12), .WR(and_1_out), .Output(sram_memory_cell_17_output));
  SRAM_Memory_Cell sram_memory_cell_30 (
    .Input(DI4), .WL(n16_bit_1_f13), .WR(and_1_out), .Output(sram_memory_cell_17_output));
  SRAM_Memory_Cell sram_memory_cell_31 (
    .Input(DI4), .WL(n16_bit_1_f14), .WR(and_1_out), .Output(sram_memory_cell_17_output));
  SRAM_Memory_Cell sram_memory_cell_32 (
    .Input(DI4), .WL(n16_bit_1_f15), .WR(and_1_out), .Output(sram_memory_cell_17_output));
  assign DO4 = and_2_out ? sram_memory_cell_17_output : 1'bz;  // Controlled_Buffer controlled_buffer_2
  SRAM_Memory_Cell sram_memory_cell_33 (
    .Input(DI3), .WL(n16_bit_1_f0), .WR(and_1_out), .Output(sram_memory_cell_33_output));
  SRAM_Memory_Cell sram_memory_cell_34 (
    .Input(DI3), .WL(n16_bit_1_f1), .WR(and_1_out), .Output(sram_memory_cell_33_output));
  SRAM_Memory_Cell sram_memory_cell_35 (
    .Input(DI3), .WL(n16_bit_1_f2), .WR(and_1_out), .Output(sram_memory_cell_33_output));
  SRAM_Memory_Cell sram_memory_cell_36 (
    .Input(DI3), .WL(n16_bit_1_f3), .WR(and_1_out), .Output(sram_memory_cell_33_output));
  SRAM_Memory_Cell sram_memory_cell_37 (
    .Input(DI3), .WL(n16_bit_1_f4), .WR(and_1_out), .Output(sram_memory_cell_33_output));
  SRAM_Memory_Cell sram_memory_cell_38 (
    .Input(DI3), .WL(n16_bit_1_f5), .WR(and_1_out), .Output(sram_memory_cell_33_output));
  SRAM_Memory_Cell sram_memory_cell_39 (
    .Input(DI3), .WL(n16_bit_1_f6), .WR(and_1_out), .Output(sram_memory_cell_33_output));
  SRAM_Memory_Cell sram_memory_cell_40 (
    .Input(DI3), .WL(n16_bit_1_f7), .WR(and_1_out), .Output(sram_memory_cell_33_output));
  SRAM_Memory_Cell sram_memory_cell_41 (
    .Input(DI3), .WL(n16_bit_1_f8), .WR(and_1_out), .Output(sram_memory_cell_33_output));
  SRAM_Memory_Cell sram_memory_cell_42 (
    .Input(DI3), .WL(n16_bit_1_f9), .WR(and_1_out), .Output(sram_memory_cell_33_output));
  SRAM_Memory_Cell sram_memory_cell_43 (
    .Input(DI3), .WL(n16_bit_1_f10), .WR(and_1_out), .Output(sram_memory_cell_33_output));
  SRAM_Memory_Cell sram_memory_cell_44 (
    .Input(DI3), .WL(n16_bit_1_f11), .WR(and_1_out), .Output(sram_memory_cell_33_output));
  SRAM_Memory_Cell sram_memory_cell_45 (
    .Input(DI3), .WL(n16_bit_1_f12), .WR(and_1_out), .Output(sram_memory_cell_33_output));
  SRAM_Memory_Cell sram_memory_cell_46 (
    .Input(DI3), .WL(n16_bit_1_f13), .WR(and_1_out), .Output(sram_memory_cell_33_output));
  SRAM_Memory_Cell sram_memory_cell_47 (
    .Input(DI3), .WL(n16_bit_1_f14), .WR(and_1_out), .Output(sram_memory_cell_33_output));
  SRAM_Memory_Cell sram_memory_cell_48 (
    .Input(DI3), .WL(n16_bit_1_f15), .WR(and_1_out), .Output(sram_memory_cell_33_output));
  assign DO3 = and_2_out ? sram_memory_cell_33_output : 1'bz;  // Controlled_Buffer controlled_buffer_3
  SRAM_Memory_Cell sram_memory_cell_49 (
    .Input(DI2), .WL(n16_bit_1_f0), .WR(and_1_out), .Output(sram_memory_cell_49_output));
  SRAM_Memory_Cell sram_memory_cell_50 (
    .Input(DI2), .WL(n16_bit_1_f1), .WR(and_1_out), .Output(sram_memory_cell_49_output));
  SRAM_Memory_Cell sram_memory_cell_51 (
    .Input(DI2), .WL(n16_bit_1_f2), .WR(and_1_out), .Output(sram_memory_cell_49_output));
  SRAM_Memory_Cell sram_memory_cell_52 (
    .Input(DI2), .WL(n16_bit_1_f3), .WR(and_1_out), .Output(sram_memory_cell_49_output));
  SRAM_Memory_Cell sram_memory_cell_53 (
    .Input(DI2), .WL(n16_bit_1_f4), .WR(and_1_out), .Output(sram_memory_cell_49_output));
  SRAM_Memory_Cell sram_memory_cell_54 (
    .Input(DI2), .WL(n16_bit_1_f5), .WR(and_1_out), .Output(sram_memory_cell_49_output));
  SRAM_Memory_Cell sram_memory_cell_55 (
    .Input(DI2), .WL(n16_bit_1_f6), .WR(and_1_out), .Output(sram_memory_cell_49_output));
  SRAM_Memory_Cell sram_memory_cell_56 (
    .Input(DI2), .WL(n16_bit_1_f7), .WR(and_1_out), .Output(sram_memory_cell_49_output));
  SRAM_Memory_Cell sram_memory_cell_57 (
    .Input(DI2), .WL(n16_bit_1_f8), .WR(and_1_out), .Output(sram_memory_cell_49_output));
  SRAM_Memory_Cell sram_memory_cell_58 (
    .Input(DI2), .WL(n16_bit_1_f9), .WR(and_1_out), .Output(sram_memory_cell_49_output));
  SRAM_Memory_Cell sram_memory_cell_59 (
    .Input(DI2), .WL(n16_bit_1_f10), .WR(and_1_out), .Output(sram_memory_cell_49_output));
  SRAM_Memory_Cell sram_memory_cell_60 (
    .Input(DI2), .WL(n16_bit_1_f11), .WR(and_1_out), .Output(sram_memory_cell_49_output));
  SRAM_Memory_Cell sram_memory_cell_61 (
    .Input(DI2), .WL(n16_bit_1_f12), .WR(and_1_out), .Output(sram_memory_cell_49_output));
  SRAM_Memory_Cell sram_memory_cell_62 (
    .Input(DI2), .WL(n16_bit_1_f13), .WR(and_1_out), .Output(sram_memory_cell_49_output));
  SRAM_Memory_Cell sram_memory_cell_63 (
    .Input(DI2), .WL(n16_bit_1_f14), .WR(and_1_out), .Output(sram_memory_cell_49_output));
  SRAM_Memory_Cell sram_memory_cell_64 (
    .Input(DI2), .WL(n16_bit_1_f15), .WR(and_1_out), .Output(sram_memory_cell_49_output));
  assign DO2 = and_2_out ? sram_memory_cell_49_output : 1'bz;  // Controlled_Buffer controlled_buffer_4
  SRAM_Memory_Cell sram_memory_cell_65 (
    .Input(DI1), .WL(n16_bit_1_f0), .WR(and_1_out), .Output(sram_memory_cell_65_output));
  SRAM_Memory_Cell sram_memory_cell_66 (
    .Input(DI1), .WL(n16_bit_1_f1), .WR(and_1_out), .Output(sram_memory_cell_65_output));
  SRAM_Memory_Cell sram_memory_cell_67 (
    .Input(DI1), .WL(n16_bit_1_f2), .WR(and_1_out), .Output(sram_memory_cell_65_output));
  SRAM_Memory_Cell sram_memory_cell_68 (
    .Input(DI1), .WL(n16_bit_1_f3), .WR(and_1_out), .Output(sram_memory_cell_65_output));
  SRAM_Memory_Cell sram_memory_cell_69 (
    .Input(DI1), .WL(n16_bit_1_f4), .WR(and_1_out), .Output(sram_memory_cell_65_output));
  SRAM_Memory_Cell sram_memory_cell_70 (
    .Input(DI1), .WL(n16_bit_1_f5), .WR(and_1_out), .Output(sram_memory_cell_65_output));
  SRAM_Memory_Cell sram_memory_cell_71 (
    .Input(DI1), .WL(n16_bit_1_f6), .WR(and_1_out), .Output(sram_memory_cell_65_output));
  SRAM_Memory_Cell sram_memory_cell_72 (
    .Input(DI1), .WL(n16_bit_1_f7), .WR(and_1_out), .Output(sram_memory_cell_65_output));
  SRAM_Memory_Cell sram_memory_cell_73 (
    .Input(DI1), .WL(n16_bit_1_f8), .WR(and_1_out), .Output(sram_memory_cell_65_output));
  SRAM_Memory_Cell sram_memory_cell_74 (
    .Input(DI1), .WL(n16_bit_1_f9), .WR(and_1_out), .Output(sram_memory_cell_65_output));
  SRAM_Memory_Cell sram_memory_cell_75 (
    .Input(DI1), .WL(n16_bit_1_f10), .WR(and_1_out), .Output(sram_memory_cell_65_output));
  SRAM_Memory_Cell sram_memory_cell_76 (
    .Input(DI1), .WL(n16_bit_1_f11), .WR(and_1_out), .Output(sram_memory_cell_65_output));
  SRAM_Memory_Cell sram_memory_cell_77 (
    .Input(DI1), .WL(n16_bit_1_f12), .WR(and_1_out), .Output(sram_memory_cell_65_output));
  SRAM_Memory_Cell sram_memory_cell_78 (
    .Input(DI1), .WL(n16_bit_1_f13), .WR(and_1_out), .Output(sram_memory_cell_65_output));
  SRAM_Memory_Cell sram_memory_cell_79 (
    .Input(DI1), .WL(n16_bit_1_f14), .WR(and_1_out), .Output(sram_memory_cell_65_output));
  SRAM_Memory_Cell sram_memory_cell_80 (
    .Input(DI1), .WL(n16_bit_1_f15), .WR(and_1_out), .Output(sram_memory_cell_65_output));
  assign DO1 = and_2_out ? sram_memory_cell_65_output : 1'bz;  // Controlled_Buffer controlled_buffer_5
  SRAM_Memory_Cell sram_memory_cell_81 (
    .Input(DI0), .WL(n16_bit_1_f0), .WR(and_1_out), .Output(sram_memory_cell_81_output));
  SRAM_Memory_Cell sram_memory_cell_82 (
    .Input(DI0), .WL(n16_bit_1_f1), .WR(and_1_out), .Output(sram_memory_cell_81_output));
  SRAM_Memory_Cell sram_memory_cell_83 (
    .Input(DI0), .WL(n16_bit_1_f2), .WR(and_1_out), .Output(sram_memory_cell_81_output));
  SRAM_Memory_Cell sram_memory_cell_84 (
    .Input(DI0), .WL(n16_bit_1_f3), .WR(and_1_out), .Output(sram_memory_cell_81_output));
  SRAM_Memory_Cell sram_memory_cell_85 (
    .Input(DI0), .WL(n16_bit_1_f4), .WR(and_1_out), .Output(sram_memory_cell_81_output));
  SRAM_Memory_Cell sram_memory_cell_86 (
    .Input(DI0), .WL(n16_bit_1_f5), .WR(and_1_out), .Output(sram_memory_cell_81_output));
  SRAM_Memory_Cell sram_memory_cell_87 (
    .Input(DI0), .WL(n16_bit_1_f6), .WR(and_1_out), .Output(sram_memory_cell_81_output));
  SRAM_Memory_Cell sram_memory_cell_88 (
    .Input(DI0), .WL(n16_bit_1_f7), .WR(and_1_out), .Output(sram_memory_cell_81_output));
  SRAM_Memory_Cell sram_memory_cell_89 (
    .Input(DI0), .WL(n16_bit_1_f8), .WR(and_1_out), .Output(sram_memory_cell_81_output));
  SRAM_Memory_Cell sram_memory_cell_90 (
    .Input(DI0), .WL(n16_bit_1_f9), .WR(and_1_out), .Output(sram_memory_cell_81_output));
  SRAM_Memory_Cell sram_memory_cell_91 (
    .Input(DI0), .WL(n16_bit_1_f10), .WR(and_1_out), .Output(sram_memory_cell_81_output));
  SRAM_Memory_Cell sram_memory_cell_92 (
    .Input(DI0), .WL(n16_bit_1_f11), .WR(and_1_out), .Output(sram_memory_cell_81_output));
  SRAM_Memory_Cell sram_memory_cell_93 (
    .Input(DI0), .WL(n16_bit_1_f12), .WR(and_1_out), .Output(sram_memory_cell_81_output));
  SRAM_Memory_Cell sram_memory_cell_94 (
    .Input(DI0), .WL(n16_bit_1_f13), .WR(and_1_out), .Output(sram_memory_cell_81_output));
  SRAM_Memory_Cell sram_memory_cell_95 (
    .Input(DI0), .WL(n16_bit_1_f14), .WR(and_1_out), .Output(sram_memory_cell_81_output));
  SRAM_Memory_Cell sram_memory_cell_96 (
    .Input(DI0), .WL(n16_bit_1_f15), .WR(and_1_out), .Output(sram_memory_cell_81_output));
  assign DO0 = and_2_out ? sram_memory_cell_81_output : 1'bz;  // Controlled_Buffer controlled_buffer_6
endmodule

module _4_Bit_decoder (
  input  A,
  input  B,
  output out_3,
  output out_4,
  output out_5,
  output out_6
);

  wire not_1_out, not_2_out;

  not not_1 (not_1_out, A);
  not not_2 (not_2_out, B);
  and and_1 (out_3, not_1_out, not_2_out);
  and and_2 (out_4, not_1_out, B);
  and and_3 (out_5, A, not_2_out);
  and and_4 (out_6, A, B);
endmodule

module _6_Bit_Adder (
  input  A5,
  input  B5,
  input  A4,
  input  B4,
  input  A3,
  input  B3,
  input  A2,
  input  B2,
  input  A1,
  input  B1,
  input  A0,
  input  B0,
  input  C,
  output Carry,
  output F0,
  output F1,
  output F2,
  output F3,
  output F4,
  output F5
);

  wire full_adder_2_f1, full_adder_3_f1, full_adder_4_f1, full_adder_5_f1, full_adder_6_f1;

  Full_Adder full_adder_1 (.A(A5), .B(B5), .C(full_adder_2_f1), .F1(Carry), .F0(F0));
  Full_Adder full_adder_2 (.A(A4), .B(B4), .C(full_adder_3_f1), .F1(full_adder_2_f1), .F0(F1));
  Full_Adder full_adder_3 (.A(A3), .B(B3), .C(full_adder_4_f1), .F1(full_adder_3_f1), .F0(F2));
  Full_Adder full_adder_4 (.A(A2), .B(B2), .C(full_adder_5_f1), .F1(full_adder_4_f1), .F0(F3));
  Full_Adder full_adder_5 (.A(A1), .B(B1), .C(full_adder_6_f1), .F1(full_adder_5_f1), .F0(F4));
  Full_Adder full_adder_6 (.A(A0), .B(B0), .C(C), .F1(full_adder_6_f1), .F0(F5));
endmodule

module Full_Adder (
  input  A,
  input  B,
  input  C,
  output F1,
  output F0
);

  wire and_1_out, and_2_out, and_3_out, and_4_out, and_5_out, and_6_out, and_7_out, not_1_out, not_2_out,
       not_3_out;

  not not_1 (not_1_out, A);
  not not_2 (not_2_out, B);
  not not_3 (not_3_out, C);
  and and_1 (and_1_out, A, B);
  and and_2 (and_2_out, A, C);
  and and_3 (and_3_out, B, C);
  and and_4 (and_4_out, A, B, C);
  and and_5 (and_5_out, not_1_out, not_2_out, C);
  and and_6 (and_6_out, not_1_out, B, not_3_out);
  and and_7 (and_7_out, A, not_2_out, not_3_out);
  or or_1 (F1, and_1_out, and_2_out, and_3_out);
  or or_2 (F0, and_4_out, and_5_out, and_6_out, and_7_out);
endmodule

module ALU (
  input  A5,
  input  A4,
  input  A3,
  input  A2,
  input  A1,
  input  A0,
  input  B5,
  input  B4,
  input  B3,
  input  B2,
  input  B1,
  input  B0,
  output F5,
  output F4,
  output F3,
  output F2,
  output F1,
  output F0
);

  wire n6_bit_adder_1_carry;

  _6_Bit_Adder u_6_bit_adder_1 (
    .A5(A5), .B5(B5), .A4(A4), .B4(B4), .A3(A3), .B3(B3), .A2(A2), .B2(B2), .A1(A1), .B1(B1), .A0(A0),
    .B0(B0), .C(1'b0), .Carry(n6_bit_adder_1_carry), .F0(F5), .F1(F4), .F2(F3), .F3(F2), .F4(F1), .F5(F0));
  // also tied to GND on the sheet: n6_bit_adder_1_carry
endmodule

module PC (
  input  Clock,
  input  D0,
  input  D1,
  input  D2,
  input  D3,
  input  Enable,
  input  Select,
  output Q0,
  output Q1,
  output Q2,
  output Q3
);

  wire multiplexer_1_out, multiplexer_2_out, multiplexer_3_out, multiplexer_4_out, n4_bit_adder_1_f0,
       n4_bit_adder_1_f1, n4_bit_adder_1_f2, n4_bit_adder_1_f3, undriven, undriven_2, undriven_3;

  _4_bit_adder u_4_bit_adder_1 (
    .A3(Q0), .B3(1'b0), .A2(Q1), .B2(1'b0), .A1(Q2), .B1(1'b0), .A0(Q3), .B0(1'b0), .C(1'b1),
    .F0(n4_bit_adder_1_f0), .F1(n4_bit_adder_1_f1), .F2(n4_bit_adder_1_f2), .F3(n4_bit_adder_1_f3));
  Multiplexer multiplexer_1 (.in0(D0), .in1(n4_bit_adder_1_f0), .out(multiplexer_1_out), .sel(Select), .en(undriven));
  D_Flip_Flop d_ff_1 (.clk(Clock), .D(multiplexer_1_out), .Q(Q0), .en(Enable));  // open: Qn, preset, reset
  D_Flip_Flop d_ff_2 (.clk(Clock), .D(multiplexer_2_out), .Q(Q1), .en(Enable));  // open: Qn, preset, reset
  Multiplexer multiplexer_2 (.in0(D1), .in1(n4_bit_adder_1_f1), .out(multiplexer_2_out), .sel(Select));  // open: en
  Multiplexer multiplexer_3 (.in0(D2), .in1(n4_bit_adder_1_f2), .out(multiplexer_3_out), .sel(Select), .en(undriven_2));
  D_Flip_Flop d_ff_3 (.clk(Clock), .D(multiplexer_3_out), .Q(Q2), .en(Enable));  // open: Qn, preset, reset
  Multiplexer multiplexer_4 (.in0(D3), .in1(n4_bit_adder_1_f3), .out(multiplexer_4_out), .sel(Select), .en(undriven_3));
  D_Flip_Flop d_ff_4 (.clk(Clock), .D(multiplexer_4_out), .Q(Q3), .en(Enable));  // open: Qn, preset, reset
endmodule

module MAR (
  input  Clock,
  input  D0,
  input  IR0,
  input  D1,
  input  IR1,
  input  D2,
  input  IR2,
  input  D3,
  input  IR3,
  input  Enable,
  input  Select,
  output Q0,
  output Q1,
  output Q2,
  output Q3
);

  wire multiplexer_1_out, multiplexer_2_out, multiplexer_3_out, multiplexer_4_out;

  Multiplexer multiplexer_1 (.in0(D0), .in1(IR0), .out(multiplexer_1_out), .sel(Select));  // open: en
  D_Flip_Flop d_ff_1 (.clk(Clock), .D(multiplexer_1_out), .Q(Q0), .en(Enable));  // open: Qn, preset, reset
  D_Flip_Flop d_ff_2 (.clk(Clock), .D(multiplexer_2_out), .Q(Q1), .en(Enable));  // open: Qn, preset, reset
  Multiplexer multiplexer_2 (.in0(D1), .in1(IR1), .out(multiplexer_2_out), .sel(Select));  // open: en
  Multiplexer multiplexer_3 (.in0(D2), .in1(IR2), .out(multiplexer_3_out), .sel(Select));  // open: en
  D_Flip_Flop d_ff_3 (.clk(Clock), .D(multiplexer_3_out), .Q(Q2), .en(Enable));  // open: Qn, preset, reset
  D_Flip_Flop d_ff_4 (.clk(Clock), .D(multiplexer_4_out), .Q(Q3), .en(Enable));  // open: Qn, preset, reset
  Multiplexer multiplexer_4 (.in0(D3), .in1(IR3), .out(multiplexer_4_out), .sel(Select));  // open: en
endmodule

module IR (
  input  Clock,
  input  D5,
  input  D4,
  input  D3,
  input  D2,
  input  D1,
  input  D0,
  input  Enable,
  output Q0,
  output Q1,
  output Q2,
  output Q3,
  output Q4,
  output Q5
);

  D_Flip_Flop d_ff_1 (.clk(Clock), .D(D5), .Q(Q0), .en(Enable));  // open: Qn, preset, reset
  D_Flip_Flop d_ff_2 (.clk(Clock), .D(D4), .Q(Q1), .en(Enable));  // open: Qn, preset, reset
  D_Flip_Flop d_ff_3 (.clk(Clock), .D(D3), .Q(Q2), .en(Enable));  // open: Qn, preset, reset
  D_Flip_Flop d_ff_4 (.clk(Clock), .D(D2), .Q(Q3), .en(Enable));  // open: Qn, preset, reset
  D_Flip_Flop d_ff_5 (.clk(Clock), .D(D1), .Q(Q4), .en(Enable));  // open: Qn, preset, reset
  D_Flip_Flop d_ff_6 (.clk(Clock), .D(D0), .Q(Q5), .en(Enable));  // open: Qn, preset, reset
endmodule

module AC (
  input  Clock,
  input  D5,
  input  D4,
  input  D3,
  input  D2,
  input  D1,
  input  D0,
  input  Enable,
  input  Reset,
  output Q0,
  output Q1,
  output Q2,
  output Q3,
  output Q4,
  output Q5
);

  D_Flip_Flop d_ff_1 (.clk(Clock), .D(D5), .Q(Q0), .en(Enable), .reset(Reset));  // open: Qn, preset
  D_Flip_Flop d_ff_2 (.clk(Clock), .D(D4), .Q(Q1), .en(Enable), .reset(Reset));  // open: Qn, preset
  D_Flip_Flop d_ff_3 (.clk(Clock), .D(D3), .Q(Q2), .en(Enable), .reset(Reset));  // open: Qn, preset
  D_Flip_Flop d_ff_4 (.clk(Clock), .D(D2), .Q(Q3), .en(Enable), .reset(Reset));  // open: Qn, preset
  D_Flip_Flop d_ff_5 (.clk(Clock), .D(D1), .Q(Q4), .en(Enable), .reset(Reset));  // open: Qn, preset
  D_Flip_Flop d_ff_6 (.clk(Clock), .D(D0), .Q(Q5), .en(Enable), .reset(Reset));  // open: Qn, preset
endmodule

module _4_bit_adder (
  input  A3,
  input  B3,
  input  A2,
  input  B2,
  input  A1,
  input  B1,
  input  A0,
  input  B0,
  input  C,
  output F0,
  output F1,
  output F2,
  output F3
);

  wire full_adder_2_f1, full_adder_3_f1, full_adder_4_f1;

  Full_Adder full_adder_1 (.A(A3), .B(B3), .C(full_adder_2_f1), .F0(F0));  // open: F1
  Full_Adder full_adder_2 (.A(A2), .B(B2), .C(full_adder_3_f1), .F1(full_adder_2_f1), .F0(F1));
  Full_Adder full_adder_3 (.A(A1), .B(B1), .C(full_adder_4_f1), .F1(full_adder_3_f1), .F0(F2));
  Full_Adder full_adder_4 (.A(A0), .B(B0), .C(C), .F1(full_adder_4_f1), .F0(F3));
endmodule

module _4_bit_register (
  input  Clock,
  input  D0,
  input  D1,
  input  D2,
  input  D3,
  output Q0,
  output Q1,
  output Q2,
  output Q3
);

  D_Flip_Flop d_ff_1 (.clk(Clock), .D(D0), .Q(Q0));  // open: Qn, preset, en, reset
  D_Flip_Flop d_ff_2 (.clk(Clock), .D(D1), .Q(Q1));  // open: Qn, preset, en, reset
  D_Flip_Flop d_ff_3 (.clk(Clock), .D(D2), .Q(Q2));  // open: Qn, preset, en, reset
  D_Flip_Flop d_ff_4 (.clk(Clock), .D(D3), .Q(Q3));  // open: Qn, preset, en, reset
endmodule

module N2 (
  input  P2,
  input  P1,
  input  P0,
  input  A,
  input  B,
  output out_6
);

  wire and_1_out, and_2_out, and_3_out, not_1_out, not_2_out, not_3_out, not_4_out, not_5_out;

  not not_1 (not_1_out, P2);
  not not_2 (not_2_out, P1);
  not not_3 (not_3_out, P0);
  not not_4 (not_4_out, A);
  and and_1 (and_1_out, not_1_out, P0, B);
  and and_2 (and_2_out, not_2_out, P0, A);
  and and_3 (and_3_out, P2, not_2_out, not_3_out, not_4_out);
  not not_5 (not_5_out, B);
  or or_1 (out_6, and_1_out, and_2_out, and_3_out);
endmodule

module N1 (
  input  P2,
  input  P1,
  input  P0,
  input  A,
  input  B,
  output out_6
);

  wire and_1_out, and_2_out, and_3_out, and_4_out, not_1_out, not_2_out, not_3_out, not_4_out, not_5_out;

  not not_1 (not_1_out, P2);
  not not_2 (not_2_out, P1);
  not not_3 (not_3_out, P0);
  not not_4 (not_4_out, A);
  not not_5 (not_5_out, B);
  and and_1 (and_1_out, not_1_out, P1, not_3_out);
  and and_2 (and_2_out, P2, not_2_out, A);
  and and_3 (and_3_out, P0, A, B);
  and and_4 (and_4_out, not_2_out, P0, not_4_out, not_5_out);
  or or_1 (out_6, and_1_out, and_2_out, and_3_out, and_4_out);
endmodule

module N0 (
  input  P2,
  input  P1,
  input  P0,
  input  A,
  input  B,
  output out_6
);

  wire and_1_out, and_2_out, not_1_out, not_2_out, not_3_out, not_4_out, not_5_out;

  not not_1 (not_1_out, P2);
  not not_2 (not_2_out, P1);
  not not_3 (not_3_out, P0);
  not not_4 (not_4_out, A);
  not not_5 (not_5_out, B);
  and and_1 (and_1_out, not_2_out, not_3_out);
  and and_2 (and_2_out, not_1_out, P1, not_3_out);
  or or_1 (out_6, and_1_out, and_2_out);
endmodule

// PC E
module PC_Enable (
  input  P2,
  input  P1,
  input  P0,
  output out_4
);

  wire and_1_out, and_2_out, and_3_out, not_1_out, not_2_out, not_3_out;

  not not_1 (not_1_out, P2);
  not not_2 (not_2_out, P1);
  not not_3 (not_3_out, P0);
  and and_1 (and_1_out, P1, P0);
  and and_2 (and_2_out, P2, P1);
  and and_3 (and_3_out, P2, P0);
  or or_1 (out_4, and_1_out, and_2_out, and_3_out);
endmodule

// PC S
module PC_SelECT (
  input  P2,
  input  P1,
  input  P0,
  output out_4
);

  wire and_1_out, and_2_out, not_1_out, not_2_out, not_3_out;

  not not_1 (not_1_out, P2);
  not not_2 (not_2_out, P1);
  not not_3 (not_3_out, P0);
  and and_1 (and_1_out, P2, P0);
  or or_1 (out_4, and_1_out, and_2_out);
  and and_2 (and_2_out, P1, P0);
endmodule

module WE (
  input  P2,
  input  P1,
  input  P0,
  output out_4
);

  wire not_1_out, not_2_out, not_3_out;

  not not_1 (not_1_out, P2);
  not not_2 (not_2_out, P1);
  not not_3 (not_3_out, P0);
  and and_1 (out_4, P2, not_2_out, P0);
endmodule

// AC R
module AC_Reset (
  input  P2,
  input  P1,
  input  P0,
  output out_4
);

  wire not_1_out, not_2_out, not_3_out;

  not not_1 (not_1_out, P2);
  not not_2 (not_2_out, P1);
  not not_3 (not_3_out, P0);
  and and_1 (out_4, not_1_out, P1, not_3_out);
endmodule

module AC_En (
  input  P2,
  input  P1,
  input  P0,
  output out_4
);

  wire not_1_out, not_2_out, not_3_out;

  not not_1 (not_1_out, P2);
  not not_2 (not_2_out, P1);
  not not_3 (not_3_out, P0);
  and and_1 (out_4, not_1_out, P1, P0);
endmodule

// IR En
module IR_EnABLE (
  input  P2,
  input  P1,
  input  P0,
  output out_4
);

  wire not_1_out, not_2_out, not_3_out;

  not not_1 (not_1_out, P2);
  not not_2 (not_2_out, P1);
  not not_3 (not_3_out, P0);
  and and_1 (out_4, not_1_out, not_2_out, P0);
endmodule

// MARS
module MAR_SelECT (
  input  P2,
  input  P1,
  input  P0,
  output out_4
);

  wire and_1_out, and_2_out, not_1_out, not_2_out, not_3_out;

  not not_1 (not_1_out, P2);
  not not_2 (not_2_out, P1);
  not not_3 (not_3_out, P0);
  and and_1 (and_1_out, P2, not_2_out, not_3_out);
  or or_1 (out_4, and_1_out, and_2_out);
  and and_2 (and_2_out, not_1_out, P1, not_3_out);
endmodule

// MARE
module MAR_EnABLE (
  input  P2,
  input  P1,
  input  P0,
  output out_4
);

  wire and_1_out, and_2_out, not_1_out, not_2_out, not_3_out;

  not not_1 (not_1_out, P2);
  not not_2 (not_2_out, P1);
  not not_3 (not_3_out, P0);
  and and_1 (and_1_out, not_1_out, not_3_out);
  or or_1 (out_4, and_1_out, and_2_out);
  and and_2 (and_2_out, not_2_out, not_3_out);
endmodule

module FSM (
  input  CLK,
  input  A,
  input  B,
  output PCE,
  output PCS,
  output WE,
  output ACR,
  output ACE,
  output IRE,
  output MARS,
  output MARE
);

  wire d_ff_1_q, d_ff_2_q, d_ff_3_q, n0_1_out_6, n1_1_out_6, n2_1_out_6;

  N2 n2_1 (.out_6(n2_1_out_6), .P2(d_ff_1_q), .P1(d_ff_2_q), .P0(d_ff_3_q), .A(A), .B(B));
  N1 n1_1 (.out_6(n1_1_out_6), .P2(d_ff_1_q), .P1(d_ff_2_q), .P0(d_ff_3_q), .A(A), .B(B));
  N0 n0_1 (.out_6(n0_1_out_6), .P2(d_ff_1_q), .P1(d_ff_2_q), .P0(d_ff_3_q), .A(A), .B(B));
  D_Flip_Flop d_ff_1 (.clk(CLK), .D(n2_1_out_6), .Q(d_ff_1_q));  // open: Qn, preset, en, reset
  D_Flip_Flop d_ff_2 (.clk(CLK), .D(n1_1_out_6), .Q(d_ff_2_q));  // open: Qn, preset, en, reset
  D_Flip_Flop d_ff_3 (.clk(CLK), .D(n0_1_out_6), .Q(d_ff_3_q));  // open: Qn, preset, en, reset
  PC_Enable pc_enable_1 (.out_4(PCE), .P2(d_ff_1_q), .P1(d_ff_2_q), .P0(d_ff_3_q));
  PC_SelECT pc_select_1 (.out_4(PCS), .P2(d_ff_1_q), .P1(d_ff_2_q), .P0(d_ff_3_q));
  WE we_1 (.out_4(WE), .P2(d_ff_1_q), .P1(d_ff_2_q), .P0(d_ff_3_q));
  AC_Reset ac_reset_1 (.out_4(ACR), .P2(d_ff_1_q), .P1(d_ff_2_q), .P0(d_ff_3_q));
  AC_En ac_en_1 (.out_4(ACE), .P2(d_ff_1_q), .P1(d_ff_2_q), .P0(d_ff_3_q));
  IR_EnABLE ir_enable_1 (.out_4(IRE), .P2(d_ff_1_q), .P1(d_ff_2_q), .P0(d_ff_3_q));
  MAR_SelECT mar_select_1 (.out_4(MARS), .P2(d_ff_1_q), .P1(d_ff_2_q), .P0(d_ff_3_q));
  MAR_EnABLE mar_enable_1 (.out_4(MARE), .P2(d_ff_1_q), .P1(d_ff_2_q), .P0(d_ff_3_q));
endmodule

module CPU_A (
  input  in_1
);

  wire ac_1_q0, ac_1_q1, ac_1_q2, ac_1_q3, ac_1_q4, ac_1_q5, alu_1_f0, alu_1_f1, alu_1_f2, alu_1_f3,
       alu_1_f4, alu_1_f5, fsm_1_ace, fsm_1_acr, fsm_1_ire, fsm_1_mare, fsm_1_mars, fsm_1_pce, fsm_1_pcs,
       fsm_1_we, ir_1_q0, ir_1_q1, ir_1_q2, ir_1_q3, ir_1_q4, ir_1_q5, mar_1_q0, mar_1_q1, mar_1_q2,
       mar_1_q3, memory_circuit_1_do0, memory_circuit_1_do1, memory_circuit_1_do2, memory_circuit_1_do3,
       memory_circuit_1_do4, memory_circuit_1_do5, multiplexer_1_out, multiplexer_2_out, pc_1_q0, pc_1_q1,
       pc_1_q2, pc_1_q3;

  Multiplexer multiplexer_1 (
    .in0(ir_1_q0), .in1(memory_circuit_1_do5), .out(multiplexer_1_out), .sel(fsm_1_ire));  // open: en
  Multiplexer multiplexer_2 (
    .in0(ir_1_q1), .in1(memory_circuit_1_do4), .out(multiplexer_2_out), .sel(fsm_1_ire));  // open: en
  FSM fsm_1 (
    .PCE(fsm_1_pce), .PCS(fsm_1_pcs), .WE(fsm_1_we), .ACR(fsm_1_acr), .ACE(fsm_1_ace), .IRE(fsm_1_ire),
    .MARS(fsm_1_mars), .MARE(fsm_1_mare), .A(multiplexer_1_out), .B(multiplexer_2_out), .CLK(in_1));
  IR ir_1 (
    .Clock(in_1), .Enable(fsm_1_ire), .Q0(ir_1_q0), .Q1(ir_1_q1), .Q2(ir_1_q2), .Q3(ir_1_q3), .Q4(ir_1_q4),
    .Q5(ir_1_q5), .D5(memory_circuit_1_do5), .D4(memory_circuit_1_do4), .D3(memory_circuit_1_do3),
    .D2(memory_circuit_1_do2), .D1(memory_circuit_1_do1), .D0(memory_circuit_1_do0));
  MAR mar_1 (
    .Clock(in_1), .Enable(fsm_1_mare), .Select(fsm_1_mars), .Q0(mar_1_q0), .Q1(mar_1_q1), .Q2(mar_1_q2),
    .Q3(mar_1_q3), .D0(pc_1_q0), .IR0(ir_1_q2), .D1(pc_1_q1), .IR1(ir_1_q3), .D2(pc_1_q2), .IR2(ir_1_q4),
    .D3(pc_1_q3), .IR3(ir_1_q5));
  PC pc_1 (
    .Clock(in_1), .D0(ir_1_q2), .D1(ir_1_q3), .D2(ir_1_q4), .D3(ir_1_q5), .Select(fsm_1_pcs), .Q0(pc_1_q0),
    .Q1(pc_1_q1), .Q2(pc_1_q2), .Q3(pc_1_q3), .Enable(fsm_1_pce));
  AC ac_1 (
    .Clock(in_1), .Enable(fsm_1_ace), .Reset(fsm_1_acr), .Q0(ac_1_q0), .Q1(ac_1_q1), .Q2(ac_1_q2),
    .Q3(ac_1_q3), .Q4(ac_1_q4), .Q5(ac_1_q5), .D5(alu_1_f5), .D4(alu_1_f4), .D3(alu_1_f3), .D2(alu_1_f2),
    .D1(alu_1_f1), .D0(alu_1_f0));
  ALU alu_1 (
    .A5(ac_1_q0), .A4(ac_1_q1), .A3(ac_1_q2), .A2(ac_1_q3), .A1(ac_1_q4), .A0(ac_1_q5),
    .B0(memory_circuit_1_do0), .B1(memory_circuit_1_do1), .B2(memory_circuit_1_do2),
    .B3(memory_circuit_1_do3), .B4(memory_circuit_1_do4), .B5(memory_circuit_1_do5), .F0(alu_1_f0),
    .F1(alu_1_f1), .F2(alu_1_f2), .F3(alu_1_f3), .F4(alu_1_f4), .F5(alu_1_f5));
  Memory_Circuit memory_circuit_1 (
    .DI5(ac_1_q0), .DI4(ac_1_q1), .DI3(ac_1_q2), .DI2(ac_1_q3), .DI1(ac_1_q4), .DI0(ac_1_q5), .A0(mar_1_q0),
    .A1(mar_1_q1), .A2(mar_1_q2), .A3(mar_1_q3), .WE_Write_Enable(fsm_1_we), .CS_Chip_Select(1'b1),
    .OE_output_enable(1'b1), .DO5(memory_circuit_1_do5), .DO4(memory_circuit_1_do4),
    .DO3(memory_circuit_1_do3), .DO2(memory_circuit_1_do2), .DO1(memory_circuit_1_do1),
    .DO0(memory_circuit_1_do0));

  // Notes on the sheet:
  //   B
endmodule
