// Logisim project Cliocked d latch.circ as structural Verilog: 10 circuits, main circuit clocked d latch
module clocked_d_latch (
  input  in_1,
  input  in_2,
  output out_3,
  output out_4
);

  wire nand_1_out, nand_2_out, nand_3_out, nand_4_out, nand_5_out, nand_6_out, not_1_out;

  nand nand_1 (nand_1_out, in_1, in_2);
  nand nand_2 (nand_2_out, nand_1_out, in_2);
  not not_1 (not_1_out, in_2);
  nand nand_3 (nand_3_out, nand_1_out, nand_4_out);
  nand nand_4 (nand_4_out, nand_3_out, nand_2_out);
  nand nand_5 (nand_5_out, nand_3_out, not_1_out);
  nand nand_6 (nand_6_out, not_1_out, nand_4_out);
  nand nand_7 (out_3, nand_5_out, out_4);
  nand nand_8 (out_4, out_3, nand_6_out);
endmodule

module _4_bit_simple_register (
  input  Dk,
  input  q1,
  input  q2,
  input  q3,
  input  q4,
  output D,
  output D_2,
  output D_3,
  output D_4
);

  D_Flip_Flop d_ff_1 (.clk(Dk), .D(q1), .Q(D_3));  // open: Qn, preset, en, reset
  D_Flip_Flop d_ff_2 (.clk(Dk), .D(q2), .Q(D_4));  // open: Qn, preset, en, reset
  D_Flip_Flop d_ff_3 (.clk(Dk), .D(q3), .Q(D));  // open: Qn, preset, en, reset
  D_Flip_Flop d_ff_4 (.clk(Dk), .D(q4), .Q(D_2));  // open: Qn, preset, en, reset
endmodule

module serial_input__parllel_output (
  input  Dk,
  input  in_2,
  output q,
  output q_2,
  output q_3,
  output q_4
);

  D_Flip_Flop d_ff_1 (.clk(Dk), .D(in_2), .Q(q_3));  // open: Qn, preset, en, reset
  D_Flip_Flop d_ff_2 (.clk(Dk), .D(q_3), .Q(q_4));  // open: Qn, preset, en, reset
  D_Flip_Flop d_ff_3 (.clk(Dk), .D(q_4), .Q(q));  // open: Qn, preset, en, reset
  D_Flip_Flop d_ff_4 (.clk(Dk), .D(q), .Q(q_2));  // open: Qn, preset, en, reset
endmodule

module d_latch (
  input  D,
  input  clk_E,
  output Q,
  output Q_not
);

  wire nand_1_out, nand_2_out;

  nand nand_1 (nand_1_out, D, clk_E);
  nand nand_2 (nand_2_out, nand_1_out, clk_E);
  nand nand_3 (Q, nand_1_out, Q_not);
  nand nand_4 (Q_not, Q, nand_2_out, nand_2_out);
endmodule

module memory_cell (
  input  data_in,
  input  read_write,
  input  Adress,
  output data_out
);

  wire and_1_out, and_2_out, controlled_buffer_1_out, d_latch_1_q, not_1_out;

  not not_1 (not_1_out, read_write);
  d_latch d_latch_1 (.D(controlled_buffer_1_out), .clk_E(and_1_out), .Q(d_latch_1_q));  // open: Q_not
  and and_1 (and_1_out, read_write, Adress);
  and and_2 (and_2_out, Adress, not_1_out);
  assign controlled_buffer_1_out = and_1_out ? data_in : 1'bz;  // Controlled_Buffer controlled_buffer_1
  assign data_out = and_2_out ? d_latch_1_q : 1'bz;  // Controlled_Buffer controlled_buffer_2
endmodule

module _16_line_decoder (
  input  A0,
  input  A1,
  input  A2,
  input  A3,
  output out_5,
  output out_6,
  output out_7,
  output out_8,
  output out_9,
  output out_10,
  output out_11,
  output out_12,
  output out_13,
  output out_14,
  output out_15,
  output out_16,
  output out_17,
  output out_18,
  output out_19,
  output out_20
);

  wire not_1_out, not_2_out, not_3_out, not_4_out;

  not not_1 (not_1_out, A0);
  not not_2 (not_2_out, A1);
  not not_3 (not_3_out, A2);
  not not_4 (not_4_out, A3);
  and _0000 (out_5, not_4_out, not_3_out, not_1_out, not_2_out);
  and _0001 (out_6, not_1_out, not_2_out, not_3_out, A3);
  and _0010 (out_7, not_1_out, not_2_out, A2, not_4_out);
  and _0011 (out_8, not_1_out, not_2_out, A2, A3);
  and _0100 (out_9, not_1_out, A1, not_3_out, not_4_out);
  and _0101 (out_10, not_1_out, A1, not_3_out, A3);
  and _0110 (out_11, not_1_out, A1, A2, not_4_out);
  and _0111 (out_12, not_1_out, A1, A2, A3);
  and _1000 (out_13, A0, not_2_out, not_3_out, not_4_out);
  and _1001 (out_14, A0, not_2_out, not_3_out, A3);
  and _1010 (out_15, A0, not_2_out, A2, not_4_out);
  and _1011 (out_16, A0, not_2_out, A2, A3);
  and _1100 (out_17, A0, A1, not_3_out, not_4_out);
  and _1101 (out_18, A0, A1, not_3_out, A3);
  and _1110 (out_19, A0, A1, A2, not_4_out);
  and _1111 (out_20, A0, A1, A2, A3);
endmodule

module sram_menmory_cell (
  input  in,
  input  Wl_enable,
  input  read_and_wirte,
  output out
);

  wire and_1_out, d_ff_1_q;

  and and_1 (and_1_out, Wl_enable, read_and_wirte);
  D_Flip_Flop d_ff_1 (.clk(and_1_out), .D(in), .Q(d_ff_1_q));  // open: Qn, preset, en, reset
  assign out = Wl_enable ? d_ff_1_q : 1'bz;  // Controlled_Buffer controlled_buffer_1
endmodule

module _2__4_line_decoder (
  input  in_1,
  input  in_2,
  output out_3,
  output out_4,
  output out_5,
  output out_6
);

  wire not_1_out, not_2_out;

  not not_1 (not_1_out, in_1);
  not not_2 (not_2_out, in_2);
  and and_1 (out_3, not_1_out, not_2_out);
  and and_2 (out_4, not_1_out, in_2);
  and and_3 (out_5, in_1, not_2_out);
  and and_4 (out_6, in_2, in_1);
endmodule

module Sram_memory_circuit (
  input  input_1,
  input  input_2,
  input  in_3,
  input  in_4,
  input  WE_write,
  input  chip_select,
  input  output_enable,
  output output_2,
  output out_put_1
);

  wire and_1_out, and_2_out, n2_4_line_decoder_1_out_3, n2_4_line_decoder_1_out_4, n2_4_line_decoder_1_out_5,
       n2_4_line_decoder_1_out_6, sram_menmory_cell_1_out, sram_menmory_cell_5_out;

  _2__4_line_decoder u_2_4_line_decoder_1 (
    .in_1(in_3), .in_2(in_4), .out_3(n2_4_line_decoder_1_out_3), .out_4(n2_4_line_decoder_1_out_4),
    .out_5(n2_4_line_decoder_1_out_5), .out_6(n2_4_line_decoder_1_out_6));
  and and_1 (and_1_out, WE_write, WE_write, chip_select);
  and and_2 (and_2_out, chip_select, output_enable);
  sram_menmory_cell sram_menmory_cell_1 (
    .in(input_1), .Wl_enable(n2_4_line_decoder_1_out_3), .read_and_wirte(and_1_out),
    .out(sram_menmory_cell_1_out));
  sram_menmory_cell sram_menmory_cell_2 (
    .in(input_1), .Wl_enable(n2_4_line_decoder_1_out_4), .read_and_wirte(and_1_out),
    .out(sram_menmory_cell_1_out));
  sram_menmory_cell sram_menmory_cell_3 (
    .in(input_1), .Wl_enable(n2_4_line_decoder_1_out_5), .read_and_wirte(and_1_out),
    .out(sram_menmory_cell_1_out));
  sram_menmory_cell sram_menmory_cell_4 (
    .in(input_1), .Wl_enable(n2_4_line_decoder_1_out_6), .read_and_wirte(and_1_out),
    .out(sram_menmory_cell_1_out));
  assign out_put_1 = and_2_out ? sram_menmory_cell_1_out : 1'bz;  // Controlled_Buffer controlled_buffer_1
  sram_menmory_cell sram_menmory_cell_5 (
    .in(input_2), .Wl_enable(n2_4_line_decoder_1_out_3), .read_and_wirte(and_1_out),
    .out(sram_menmory_cell_5_out));
  sram_menmory_cell sram_menmory_cell_6 (
    .in(input_2), .Wl_enable(n2_4_line_decoder_1_out_4), .read_and_wirte(and_1_out),
    .out(sram_menmory_cell_5_out));
  sram_menmory_cell sram_menmory_cell_7 (
    .in(input_2), .Wl_enable(n2_4_line_decoder_1_out_5), .read_and_wirte(and_1_out),
    .out(sram_menmory_cell_5_out));
  sram_menmory_cell sram_menmory_cell_8 (
    .in(input_2), .Wl_enable(n2_4_line_decoder_1_out_6), .read_and_wirte(and_1_out),
    .out(sram_menmory_cell_5_out));
  assign output_2 = and_2_out ? sram_menmory_cell_5_out : 1'bz;  // Controlled_Buffer controlled_buffer_2
endmodule

module _16 (
  input  A0,
  input  A1,
  input  A2,
  input  A3,
  input  data_input,
  input  read_and_wirte,
  output out_7
);

  wire n16_line_decoder_1_out_5, n16_line_decoder_1_out_6, n16_line_decoder_1_out_7,
       n16_line_decoder_1_out_8, n16_line_decoder_1_out_9, n16_line_decoder_1_out_10,
       n16_line_decoder_1_out_11, n16_line_decoder_1_out_12, n16_line_decoder_1_out_13,
       n16_line_decoder_1_out_14, n16_line_decoder_1_out_15, n16_line_decoder_1_out_16,
       n16_line_decoder_1_out_17, n16_line_decoder_1_out_18, n16_line_decoder_1_out_19,
       n16_line_decoder_1_out_20;

  _16_line_decoder u_16_line_decoder_1 (
    .A0(A3), .A1(A2), .A2(A1), .A3(A0), .out_5(n16_line_decoder_1_out_5), .out_6(n16_line_decoder_1_out_6),
    .out_7(n16_line_decoder_1_out_7), .out_8(n16_line_decoder_1_out_8), .out_9(n16_line_decoder_1_out_9),
    .out_10(n16_line_decoder_1_out_10), .out_11(n16_line_decoder_1_out_11),
    .out_12(n16_line_decoder_1_out_12), .out_13(n16_line_decoder_1_out_13),
    .out_14(n16_line_decoder_1_out_14), .out_15(n16_line_decoder_1_out_15),
    .out_16(n16_line_decoder_1_out_16), .out_17(n16_line_decoder_1_out_17),
    .out_18(n16_line_decoder_1_out_18), .out_19(n16_line_decoder_1_out_19), .out_20(n16_line_decoder_1_out_20));
  memory_cell memory_cell_1 (
    .read_write(read_and_wirte), .Adress(n16_line_decoder_1_out_5), .data_out(out_7), .data_in(data_input));
  memory_cell memory_cell_2 (
    .read_write(read_and_wirte), .Adress(n16_line_decoder_1_out_6), .data_out(out_7), .data_in(data_input));
  memory_cell memory_cell_3 (
    .read_write(read_and_wirte), .Adress(n16_line_decoder_1_out_7), .data_out(out_7), .data_in(data_input));
  memory_cell memory_cell_4 (
    .read_write(read_and_wirte), .Adress(n16_line_decoder_1_out_8), .data_out(out_7), .data_in(data_input));
  memory_cell memory_cell_5 (
    .read_write(read_and_wirte), .Adress(n16_line_decoder_1_out_9), .data_out(out_7), .data_in(data_input));
  memory_cell memory_cell_6 (
    .read_write(read_and_wirte), .Adress(n16_line_decoder_1_out_10), .data_out(out_7), .data_in(data_input));
  memory_cell memory_cell_7 (
    .read_write(read_and_wirte), .Adress(n16_line_decoder_1_out_11), .data_out(out_7), .data_in(data_input));
  memory_cell memory_cell_8 (
    .read_write(read_and_wirte), .Adress(n16_line_decoder_1_out_12), .data_out(out_7), .data_in(data_input));
  memory_cell memory_cell_9 (
    .read_write(read_and_wirte), .Adress(n16_line_decoder_1_out_13), .data_out(out_7), .data_in(data_input));
  memory_cell memory_cell_10 (
    .read_write(read_and_wirte), .Adress(n16_line_decoder_1_out_14), .data_out(out_7), .data_in(data_input));
  memory_cell memory_cell_11 (
    .read_write(read_and_wirte), .Adress(n16_line_decoder_1_out_15), .data_out(out_7), .data_in(data_input));
  memory_cell memory_cell_12 (
    .read_write(read_and_wirte), .Adress(n16_line_decoder_1_out_16), .data_out(out_7), .data_in(data_input));
  memory_cell memory_cell_13 (
    .Adress(n16_line_decoder_1_out_17), .data_out(out_7), .data_in(data_input));  // open: read_write
  memory_cell memory_cell_14 (
    .read_write(read_and_wirte), .Adress(n16_line_decoder_1_out_18), .data_out(out_7), .data_in(data_input));
  memory_cell memory_cell_15 (
    .read_write(read_and_wirte), .Adress(n16_line_decoder_1_out_19), .data_out(out_7), .data_in(data_input));
  memory_cell memory_cell_16 (
    .read_write(read_and_wirte), .Adress(n16_line_decoder_1_out_20), .data_out(out_7), .data_in(data_input));
endmodule
