// Logisim project pop machine.circ as structural Verilog: 6 circuits, main circuit main
module main (
  input  coin,
  input  refund,
  input  clock,
  output \return ,
  output pop
);

  wire d_ff_1_q, d_ff_2_q, d_ff_3_q, n0_1_out_6, n1_1_out_6, n2_1_out_6;

  N2 n2_1 (.P2(d_ff_2_q), .P1(d_ff_1_q), .P0(d_ff_3_q), .A(refund), .B(coin), .out_6(n2_1_out_6));
  N1 n1_1 (.P2(d_ff_2_q), .P1(d_ff_1_q), .P0(d_ff_3_q), .A(refund), .B(coin), .out_6(n1_1_out_6));
  N0 n0_1 (.P2(d_ff_2_q), .P1(d_ff_1_q), .P0(d_ff_3_q), .A(refund), .B(coin), .out_6(n0_1_out_6));
  D_Flip_Flop d_ff_1 (.clk(clock), .D(n1_1_out_6), .Q(d_ff_1_q));  // open: Qn, preset, en, reset
  D_Flip_Flop d_ff_2 (.clk(clock), .D(n2_1_out_6), .Q(d_ff_2_q));  // open: Qn, preset, en, reset
  D_Flip_Flop d_ff_3 (.clk(clock), .D(n0_1_out_6), .Q(d_ff_3_q));  // open: Qn, preset, en, reset
  F1 f1_1 (.P2(d_ff_2_q), .P1(d_ff_1_q), .P0(d_ff_3_q), .F1(\return ));
  F0 f0_1 (.in_1(d_ff_2_q), .P1(d_ff_1_q), .P0(d_ff_3_q), .F0(pop));
endmodule

module N2 (
  input  P2,
  input  P1,
  input  P0,
  input  A,
  input  B,
  output out_6
);

  wire and_1_out, and_2_out, and_3_out, and_4_out, not_1_out, not_2_out, not_3_out, not_4_out, not_5_out;

  not not_1 (not_1_out, P2);
  not not_2 (not_2_out, P1);
  not not_3 (not_3_out, P0);
  not not_4 (not_4_out, A);
  not not_5 (not_5_out, B);
  and and_1 (and_1_out, P0, A);
  and and_2 (and_2_out, P1, A);
  and and_3 (and_3_out, P2, A);
  and and_4 (and_4_out, B, P1, P0);
  or or_1 (out_6, and_1_out, and_2_out, and_3_out, and_4_out);
endmodule

module N1 (
  input  P2,
  input  P1,
  input  P0,
  input  A,
  input  B,
  output out_6
);

  wire and_1_out, and_2_out, and_3_out, not_1_out, not_2_out, not_3_out, not_4_out, not_5_out;

  not not_1 (not_1_out, P2);
  not not_2 (not_2_out, P1);
  not not_3 (not_3_out, P0);
  not not_4 (not_4_out, A);
  not not_5 (not_5_out, B);
  and and_1 (and_1_out, not_1_out, not_2_out, P0, not_4_out, B);
  and and_2 (and_2_out, P1, not_4_out, not_5_out);
  and and_3 (and_3_out, P1, not_3_out, not_4_out);
  or or_1 (out_6, and_1_out, and_2_out, and_3_out);
endmodule

module N0 (
  input  P2,
  input  P1,
  input  P0,
  input  A,
  input  B,
  output out_6
);

  wire and_1_out, and_2_out, and_3_out, and_4_out, and_5_out, and_6_out, not_1_out, not_2_out, not_3_out,
       not_4_out, not_5_out;

  not not_1 (not_1_out, P2);
  not not_2 (not_2_out, P1);
  not not_3 (not_3_out, P0);
  not not_4 (not_4_out, A);
  not not_5 (not_5_out, B);
  and and_1 (and_1_out, P0, A);
  and and_2 (and_2_out, P1, A);
  and and_3 (and_3_out, P2, B);
  and and_4 (and_4_out, P2, A);
  and and_5 (and_5_out, not_1_out, P0, not_5_out);
  and and_6 (and_6_out, not_3_out, not_4_out, B);
  or or_1 (out_6, and_1_out, and_2_out, and_3_out, and_4_out, and_5_out, and_6_out);
endmodule

module F1 (
  input  P2,
  input  P1,
  input  P0,
  output F1
);

  wire and_1_out, not_1_out, not_2_out, not_3_out;

  not not_1 (not_1_out, P2);
  not not_2 (not_2_out, P1);
  not not_3 (not_3_out, P0);
  and and_1 (and_1_out, P2, not_2_out, P0);
  buf or_1 (F1, and_1_out);  // OR_Gate
endmodule

module F0 (
  input  in_1,
  input  P1,
  input  P0,
  output F0
);

  wire and_1_out, not_1_out, not_2_out, not_3_out;

  not not_1 (not_1_out, in_1);
  not not_2 (not_2_out, P1);
  not not_3 (not_3_out, P0);
  and and_1 (and_1_out, in_1, not_2_out, not_3_out);
  buf or_1 (F0, and_1_out);  // OR_Gate
endmodule
